# Fritzing sketch hardware-design (saved by Fritzing 0.9.3b)

parts:
  NODE_MCU_8266 = ESP8266 NodeMCU LoLin module
  VOLTAGE_SENSOR = zmpt101b
  12V_BATTERY = 4 x AAA Battery Mount
  Part1 = Current Sensor 5A
  A1 = sim900 generic
  BUZZER = Piezo Speaker
  WARNING_LED = LED - 3mm [color="Red (633nm)" package="3 mm [THT]"]
  SUCCESS_LED = LED - 3mm [color="Green (560nm)" package="3 mm [THT]"]
  R1 = Resistor [tolerance=±5% resistance=220 package="2010 [SMD]"]
  R2 = Resistor [tolerance=±5% resistance=220 package="2010 [SMD]"]
  MAGNITIC_LOCK = SWITCH-MOMENTARY-2 [package=reed_switch_plastic]
  R3 = Resistor [tolerance=±5% resistance=220 package="2512 [SMD]"]
  LCD_DISPLAY = LCD1602-I2C

nets:
  N1: NODE_MCU_8266.D0, R2.Pin_1
  N2: NODE_MCU_8266.D1, R3.Pin_0
  N3: NODE_MCU_8266.D2, R1.Pin_1
  N4: NODE_MCU_8266.D3, LCD_DISPLAY.SCL
  N5: NODE_MCU_8266.D4, LCD_DISPLAY.SDA
  VCC: NODE_MCU_8266.3V3, VOLTAGE_SENSOR.VCC, Part1.VCC
  GND: NODE_MCU_8266.GND, VOLTAGE_SENSOR.GND, 12V_BATTERY.-, Part1.GND, BUZZER.pin1, WARNING_LED.cathode, SUCCESS_LED.cathode, MAGNITIC_LOCK.2, LCD_DISPLAY.GND
  N6: NODE_MCU_8266.D6, BUZZER.pin2
  N7: NODE_MCU_8266.D7, Part1.OUT
  N8: NODE_MCU_8266.D8, VOLTAGE_SENSOR.OUT
  N9: NODE_MCU_8266.RX, A1.Pin_40
  N10: NODE_MCU_8266.TX, A1.Pin_45
  VIN: NODE_MCU_8266.Vin, 12V_BATTERY.+, LCD_DISPLAY.VCC
  N11: WARNING_LED.anode, R1.Pin_0
  N12: SUCCESS_LED.anode, R2.Pin_0
  N13: MAGNITIC_LOCK.1, R3.Pin_1

custom parts:
  ESP8266 NodeMCU LoLin module: ESP8266 based NodeMCU
  zmpt101b: Single phase ac active output voltate transformer module.
  sim900 generic: sim900 generic one instance of the generic (i.e. not one of the Seeed boards) sim900 modules. It matches the specific board this person has but may do for the general generic sim900 modules.
  LCD1602-I2C: A standard character display, usually with 2x16 characters. Comes in many colors with LCM1602 IIC attached.
